// Digital circuit CPU.dig as structural Verilog
module CPU (
  input  clock
);

  wire branchControl_d;
  wire [0:0] execution_unit_zero;
  wire [1:0] reg_file_p3;
  wire [10:0] MainControl_d;
  wire [15:0] bitextender_1_out, branch_unit_r, data_d, execution_unit_r, instructionReg_d,
       multiplexer_1_out, multiplexer_2_out, pc_incrementer_r, programCounter_q, reg_file_p4, reg_file_p7,
       reg_file_p8, shift_left_1_1_out;

  D_FF #(.Bits(16)) programCounter (.D(multiplexer_1_out), .C(~clock), .Q(programCounter_q));  // open: nQ
  Multiplexer #(.Bits(16)) multiplexer_1 (
    .sel(branchControl_d), .in_0(pc_incrementer_r), .in_1(branch_unit_r), .out(multiplexer_1_out));
  ALU pc_incrementer (.r(pc_incrementer_r), .a(programCounter_q), .b(16'h2), .s(4'b0010));  // open: zero, overflow
  ROM #(.AddrBits(16), .Bits(16)) instructionReg (.A(programCounter_q), .sel(1'b1), .D(instructionReg_d));
  ROM #(.AddrBits(4), .Bits(11)) MainControl (.A(instructionReg_d[15:12]), .sel(1'b1), .D(MainControl_d));
  // reg_file reg_file: pin names not known; wires that end beside it: instructionReg_d[11:10], instructionReg_d[9:8], reg_file_p3, reg_file_p4, MainControl_d[7], clock, reg_file_p7, reg_file_p8
  BitExtender bitextender_1 (.in(instructionReg_d[7:0]), .out(bitextender_1_out));
  shift_left_1 shift_left_1_1 (.in(bitextender_1_out), .out(shift_left_1_1_out));
  Multiplexer #(.Bits(16)) multiplexer_2 (
    .sel(MainControl_d[9]), .in_0(reg_file_p8), .in_1(bitextender_1_out), .out(multiplexer_2_out));
  Multiplexer #(.Bits(2)) multiplexer_3 (
    .sel(MainControl_d[10]), .in_0(instructionReg_d[9:8]), .in_1(instructionReg_d[7:6]), .out(reg_file_p3));
  ALU branch_unit (
    .r(branch_unit_r), .a(pc_incrementer_r), .b(shift_left_1_1_out), .s(4'b0010));  // open: zero, overflow
  ALU execution_unit (
    .zero(execution_unit_zero[0]), .r(execution_unit_r), .a(reg_file_p7), .b(multiplexer_2_out),
    .s(MainControl_d[3:0]));  // open: overflow
  ROM #(.AddrBits(3)) branchControl (.A({MainControl_d[5:4], execution_unit_zero[0]}), .sel(1'b1), .D(branchControl_d));
  BlockRAMDualPort #(.AddrBits(16), .Bits(16)) data (
    .A(execution_unit_r), .Din(reg_file_p8), .str(MainControl_d[6]), .C(clock), .D(data_d));
  Multiplexer #(.Bits(16)) multiplexer_4 (
    .sel(MainControl_d[8]), .in_0(execution_unit_r), .in_1(data_d), .out(reg_file_p4));

  // Notes on the sheet:
  //   contents of instructionReg (hex, n*v repeats v):
  //   7407,0,7803,0,9100,0,9202,0,8100,0,8202,0,66c0,0,ac02,0,9102,0
  //   ,9200,0,8100,0,8202,0,4a80,0,7a01,0,6c0
  //   IF/ID
  //   contents of MainControl (hex, n*v repeats v):
  //   482,486,480,481,48c,48d,487,282,382,242,26,16
  //   TODO bit
  //   ordering
  //   ID/EX
  //   beq
  //   bne
  //   RegWrite
  //   MemToReg
  //   MemWrite
  //   RegDest
  //   ALUsrc
  //   ALUctl
  //   nextBranch
  //   muxData
  //   muxReg
  //   EX/MA
  //   contents of branchControl (hex, n*v repeats v):
  //   0,1
  //   PCSrc
  //   MA/WB
  //   muxWriteReg
endmodule
